# Fritzing sketch PracticeSketch (saved by Fritzing 0.9.4)
breadboards: 1

parts:
  U1 = 7400 4 x 2 Input NAND Gate [part_number=7400 package="DIP (Dual Inline) [THT]"]
  U2 = 7400 4 x 2 Input NAND Gate [part_number=7400 package="DIP (Dual Inline) [THT]"]

nets:
  N1: U1.A2, U2.A1
  N2: U1.B2, U1.B3
  GND: U1.GND, U2.GND
  N3: U1.Q3, U1.Q4
  VDD: U1.A4, U1.VDD, U2.Q1, U2.VDD
  N4: U2.Q2, U2.A2
  N5: U2.B2, U2.B3

notes:
  GND
